// Logisim project logisim_05_splitters.circ as structural Verilog: 1 circuit, main circuit inputs_with_8_bits
module inputs_with_8_bits (
  input  [7:0] in_1,
  input  [7:0] in_2,
  input  [7:0] in_3,
  input  [7:0] in_4,
  input  in_5,
  input  in_6,
  input  in_7,
  input  in_8,
  input  in_9,
  input  in_10,
  input  in_11,
  input  in_12,
  output [7:0] out_13
);


  assign out_13 = {in_12, in_11, in_10, in_9, in_8, in_7, in_6, in_5};
endmodule
