// Logisim project logisim_blocks_use_object_properties.circ as structural Verilog: 3 circuits, main circuit and_with_24_inputs
module and_with_24_inputs (
);

  // AND_Gate and_1 is placed but not wired
endmodule

module input_bits_vector (
  input  [7:0] in_1
);
endmodule

module and_with_bits_vectors (
  input  [3:0] in_1,
  input  [3:0] in_2,
  output [3:0] out_3
);

  assign out_3 = in_1 & in_2;  // AND_Gate and_1, 4 bits wide
endmodule
