// Logisim project logisim_cables_chaotic_addition_circuit.circ as structural Verilog: 3 circuits, main circuit chaotic
module chaotic (
  input  A,
  input  B,
  input  carry,
  output result,
  output remainder
);

  wire and_1_out, not_1_out, not_2_out, not_3_out, xor_1_out, xor_2_out;

  not not_1 (not_1_out, A);
  not not_2 (not_2_out, carry);
  not not_3 (not_3_out, B);
  and and_1 (and_1_out, A, B, carry);
  ExactlyOne xor_1 (.out(xor_1_out), .in0(A), .in1(B), .in2(B));
  ExactlyOne xor_2 (.out(xor_2_out), .in0(not_1_out), .in1(not_2_out), .in2(not_3_out));
  or or_1 (result, and_1_out, xor_1_out);
  or or_2 (remainder, and_1_out, xor_2_out);
endmodule

module sorted (
  input  A,
  input  B,
  input  carry,
  output result,
  output remainder
);

  wire and_1_out, not_1_out, not_2_out, not_3_out, not_4_out, not_5_out, not_6_out, xor_1_out, xor_2_out;

  not not_1 (not_1_out, A);
  not not_2 (not_2_out, B);
  not not_3 (not_3_out, carry);
  and and_1 (and_1_out, A, B, carry);
  ExactlyOne xor_1 (.out(xor_1_out), .in0(A), .in1(B), .in2(carry));
  ExactlyOne xor_2 (.out(xor_2_out), .in0(not_1_out), .in1(not_2_out), .in2(not_3_out));
  not not_4 (not_4_out, and_1_out);
  not not_5 (not_5_out, xor_1_out);
  not not_6 (not_6_out, xor_2_out);
  or or_1 (result, and_1_out, xor_1_out);
  or or_2 (remainder, and_1_out, xor_2_out);
endmodule

module error (
  input  A,
  input  B,
  input  carry,
  output result,
  output remainder
);

  wire and_1_out, not_1_out, not_2_out, not_3_out, xor_1_out, xor_2_out;

  not not_1 (not_1_out, A);
  not not_2 (not_2_out, B);
  not not_3 (not_3_out, carry);
  and and_1 (and_1_out, A, B, carry);
  ExactlyOne xor_1 (.out(xor_1_out), .in0(A), .in1(B), .in2(carry));
  ExactlyOne xor_2 (.out(xor_2_out), .in0(not_1_out), .in1(not_2_out), .in2(not_3_out));
  not not_4 (xor_2_out, and_1_out);
  not not_5 (xor_2_out, xor_1_out);
  not not_6 (xor_2_out, xor_2_out);
  or or_1 (result, and_1_out, xor_1_out);
  or or_2 (remainder, and_1_out, xor_2_out);
endmodule
