// Logisim project logisim_dff.circ as structural Verilog: 1 circuit, main circuit main
module main (
  input  InputBit,
  output OutputBit
);

  wire ClockComponent_out, Reset_out, Set_out;

  Clock ClockComponent (.out(ClockComponent_out));
  Button Set (.out(Set_out));
  D_Flip_Flop d_ff_1 (
    .D(InputBit), .clk(ClockComponent_out), .Q(OutputBit), .preset(Set_out), .reset(Reset_out));  // open: Qn
  Button Reset (.out(Reset_out));
endmodule
