// Logisim project logisim_subcircuits.circ as structural Verilog
module and_gate (
  input  A,
  input  B,
  output Y
);

  and and_1 (Y, A, B);
endmodule

module example_with_and_gate (
  input  in_1,
  input  in_2,
  output out_3
);

  and_gate and_gate_1 (.A(in_1), .B(in_2), .Y(out_3));
endmodule

module complete_example_circuit (
  input  [1:0] in_1,
  input  [1:0] in_2
);

  wire [7:0] complete_example_converter_2_converted;

  // complete_example_converter complete_example_converter_1: pin names not known; wires that end beside it: in_1
  complete_example_converter complete_example_converter_2 (
    .number(in_2), .converted(complete_example_converter_2_converted));
  _7_Segment_Display u_7_segment_display_1 ();  // open: g, f, a, b, e, d, c, dp
  _7_Segment_Display u_7_segment_display_2 (
    .g(complete_example_converter_2_converted[7]), .f(complete_example_converter_2_converted[6]),
    .a(complete_example_converter_2_converted[5]), .b(complete_example_converter_2_converted[4]),
    .e(complete_example_converter_2_converted[0]), .d(complete_example_converter_2_converted[1]),
    .c(complete_example_converter_2_converted[2]), .dp(complete_example_converter_2_converted[3]));
endmodule

module complete_example_converter (
  input  [1:0] number,
  output [7:0] converted
);

  wire not_1_out;

  not not_1 (not_1_out, number[1]);
  not not_2 (converted[0], number[0]);
  and and_1 (converted[6], not_1_out, converted[0]);
  or or_1 (converted[5], converted[0], number[1]);
  or or_2 (converted[2], not_1_out, number[0]);
  or or_3 (converted[1], converted[0], number[1]);

  assign {converted[7], converted[4:3]} = {number[1], 2'b10};
endmodule
