// Logisim project logisim_truth_tables_generate_circuits_with_truth_tables.circ as structural Verilog
module bits_addition (
  input  A,
  input  B,
  input  carry,
  output result,
  output remainder
);

  wire and_1_out, and_2_out, and_3_out, and_4_out, and_5_out, and_6_out, and_7_out, not_1_out, not_2_out,
       not_3_out;

  not not_1 (not_1_out, A);
  not not_2 (not_2_out, B);
  not not_3 (not_3_out, carry);
  and and_1 (and_1_out, not_1_out, not_2_out, carry);
  and and_2 (and_2_out, not_1_out, B, not_3_out);
  and and_3 (and_3_out, A, not_2_out, not_3_out);
  and and_4 (and_4_out, A, B, carry);
  and and_5 (and_5_out, B, carry);
  and and_6 (and_6_out, A, carry);
  and and_7 (and_7_out, A, B);
  or or_1 (result, and_1_out, and_2_out, and_3_out, and_4_out);
  or or_2 (remainder, and_5_out, and_6_out, and_7_out);
endmodule
