// Logisim project logisim_7_segments_display.circ as structural Verilog: 1 circuit, main circuit main
module main (
);

  _7_Segment_Display u_7_segment_display_1 ();  // open: g, f, a, b, e, d, c, dp
  _7_Segment_Display u_7_segment_display_2 (.g(1'b1));  // open: f, a, b, e, d, c, dp
  _7_Segment_Display u_7_segment_display_3 (.e(1'b1));  // open: g, f, a, b, d, c, dp
  _7_Segment_Display u_7_segment_display_4 (.a(1'b1));  // open: g, f, b, e, d, c, dp
  _7_Segment_Display u_7_segment_display_5 (.f(1'b1));  // open: g, a, b, e, d, c, dp
  _7_Segment_Display u_7_segment_display_6 (.c(1'b1));  // open: g, f, a, b, e, d, dp
  _7_Segment_Display u_7_segment_display_7 (.d(1'b1));  // open: g, f, a, b, e, c, dp
  _7_Segment_Display u_7_segment_display_8 (.g(1'b1), .b(1'b1), .c(1'b1), .dp(1'b1));  // open: f, a, e, d
  _7_Segment_Display u_7_segment_display_9 (.b(1'b1));  // open: g, f, a, e, d, c, dp
  _7_Segment_Display u_7_segment_display_10 (.dp(1'b1));  // open: g, f, a, b, e, d, c
endmodule
